# Fritzing sketch garvuino_09g_breadboard_only (saved by Fritzing 0.9.3b)
breadboards: 1

parts:
  24_Mhz = Crystal [frequency="25 MHz" package=THT]
  Arduino_Nano = Arduino Nano (Rev3.0)
  R4 = Resistor [tolerance=±5% resistance=10k package=THT]
  C6 = Electrolytic Capacitor [capacitance=10µF package="100 mil [THT, electrolytic]"]
  R5 = Resistor [tolerance=±5% resistance=10k package=THT]
  C3 = Electrolytic Capacitor [capacitance=10µF package="100 mil [THT, electrolytic]"]
  C2 = Ceramic Capacitor [capacitance=820pF voltage=6.3V package="100 mil [THT, multilayer]"]
  C7 = Ceramic Capacitor [capacitance=820pF voltage=6.3V package="100 mil [THT, multilayer]"]
  Switch = Momentary Switch [package=ksa_sealed_tac_switch]
  midi = MIDI_CONN_FEMALE_SUPPORT [package=din_5_female_support]
  TRS = Audio Jack (TRS) 3.5mm [package="4Ucon 08780 [THT]"]
  LED1 = LED - 5mm [color="Red (633nm)" package="5 mm [THT]"]
  R3 = Resistor [tolerance=±5% resistance=1k package=THT]
  sd = MicroSD Card Module
  J4 = male pin header, 8 pins [form="♂ (male)"]
  IC1 = ATMEGA8 [package=DIL]

nets:
  N1: 24_Mhz.pin_0, IC1.PB6
  N2: 24_Mhz.pin_1, IC1.PB7
  N3: Arduino_Nano.D1/TX, IC1.PD0
  N4: Arduino_Nano.D0/RX, midi.NC2, midi.MIDI_IN
  GND: Arduino_Nano.GND, C2.0, C7.0, Switch.1, midi.NC1, TRS.Sleeve, LED1.cathode, sd.GND, J4.pin1, IC1.GND#8
  N5: Arduino_Nano.D4, sd.CS, J4.pin4
  N6: Arduino_Nano.D6, Switch.3
  N7: Arduino_Nano.D8, R3.Pin_1
  N8: Arduino_Nano.D9, R5.Pin_1, IC1.PB1
  N9: Arduino_Nano.D11/MOSI, sd.MOSI, J4.pin5
  N10: Arduino_Nano.D12/MISO, sd.MISO, J4.pin7
  5V: Arduino_Nano.5V, IC1.VCC
  N11: Arduino_Nano.D13/SCK, sd.SCK, J4.pin6
  N12: R4.Pin_0, C6.+, C2.1
  N13: R4.Pin_1, IC1.PB2
  N14: C6.-, TRS.Ring
  N15: R5.Pin_0, C3.+, C7.1
  N16: C3.-, TRS.Tip
  N17: LED1.anode, R3.Pin_0
  N18: sd.VCC, J4.pin3

notes:
  chiptune player v1.09
  midi
  mini usb
  www.avray.ru
  garvalf.online.fr
  GND
  5V
  CS
  MOSI
  SCK
  MISO
  SD card reader
  R
  L
  full SD reader
  micro SD reader
